// Logisim project circuito_vetorial.circ as structural Verilog: 6 circuits, main circuit main
module main (
);

  wire adder_1_cout, and_1_out, Branch, CLK, comparator_1_gt, comparator_1_lt, Inc, Reset, S_WE, S_WR, Sel_H,
       V_WE, V_WR, W_SR1, W_VR1, Zero;
  wire [1:0] ALUOp, DataToReg, multiplexer_3_out, S_RA, S_RB, V_RA, V_RB, V_RD;
  wire [3:0] Imm, Opcode;
  wire [7:0] adder_1_out, MemDados_S_dout, MemDados_V0_dout, MemDados_V1_dout, MemDados_V2_dout,
       MemDados_V3_dout, MemInstrucao_data, move_1_movh, move_1_movl, move_2_movh, move_2_movl, move_3_movh,
       move_3_movl, move_4_movh, move_4_movl, move_5_movh, move_5_movl, multiplexer_1_out, multiplexer_4_out,
       multiplexer_5_out, multiplexer_6_out, multiplexer_7_out, multiplexer_13_out, multiplexer_14_out,
       multiplexer_15_out, multiplexer_16_out, multiplexer_17_out, PC_q, S_DRA, S_DRB, S_Mov, ula_1_s,
       ula_2_s, ula_3_s, ula_4_s, ula_5_s, V_DRA0, V_DRA1, V_DRA2, V_DRA3, V_DRB0, V_DRB1, V_DRB2, V_DRB3,
       V_Mov0, V_Mov1, V_Mov2, V_Mov3;

  Adder adder_1 (.a(PC_q), .b(8'h1), .out(adder_1_out), .cin(1'b0), .cout(adder_1_cout));
  LED led_1 (.in(adder_1_cout));
  Button button_1 (.out(Reset));
  Clock clock_1 (.out(CLK));
  and and_1 (and_1_out, Branch, Zero);
  ROM #(.addrWidth(4), .dataWidth(13)) MemControle (
    .addr(Opcode), .data({ALUOp, Branch, DataToReg, W_SR1, W_VR1, S_WR, V_WR, Sel_H, S_WE, V_WE, Inc}));
  // Probe on multiplexer_1_out
  Multiplexer #(.width(8)) multiplexer_1 (.in0(adder_1_out), .in1(S_DRB), .out(multiplexer_1_out), .sel(and_1_out));
  Multiplexer #(.width(2)) multiplexer_2 (.in0(V_RA), .in1(2'b01), .out(V_RD), .sel(W_VR1));
  Register PC (.D(multiplexer_1_out), .en(1'b1), .clk(CLK), .Q(PC_q), .clr(Reset));
  // Probe on PC_q
  ROM MemInstrucao (.addr(PC_q), .data(MemInstrucao_data));
  Decodificador decodificador_1 (
    .Inst(MemInstrucao_data), .Opcode(Opcode), .Imm(Imm), .S_RA(S_RA), .V_RA(V_RA), .S_RB(S_RB), .V_RB(V_RB));
  // Probe on Opcode
  Multiplexer #(.width(2)) multiplexer_3 (.in0(S_RA), .in1(2'b01), .out(multiplexer_3_out), .sel(W_SR1));
  BR_vet br_vet_1 (
    .RB(V_RB), .WriteReg(V_WR), .RW(V_RD), .Reset(Reset), .Clk(CLK), .Dados(multiplexer_14_out),
    .VR0({8{1'b0}}), .RA(V_RD), .DRB(V_DRB0), .DRA(V_DRA0));
  BR_vet br_vet_2 (
    .RB(V_RB), .WriteReg(V_WR), .RW(V_RD), .Reset(Reset), .Clk(CLK), .Dados(multiplexer_15_out), .VR0(8'h1),
    .RA(V_RD), .DRB(V_DRB1), .DRA(V_DRA1));
  BR_vet br_vet_3 (
    .RB(V_RB), .WriteReg(V_WR), .RW(V_RD), .Reset(Reset), .Clk(CLK), .Dados(multiplexer_16_out), .VR0(8'h2),
    .RA(V_RD), .DRB(V_DRB2), .DRA(V_DRA2));
  BR_vet br_vet_4 (
    .RB(V_RB), .WriteReg(V_WR), .RW(V_RD), .Reset(Reset), .Clk(CLK), .Dados(multiplexer_17_out), .VR0(8'h3),
    .RA(V_RD), .DRB(V_DRB3), .DRA(V_DRA3));
  // Probe on V_DRA0
  // Probe on V_DRB0
  // Probe on V_DRA1
  // Probe on V_DRB1
  // Probe on V_DRA2
  // Probe on V_DRB2
  // Probe on V_DRA3
  // Probe on V_DRB3
  BR_seq br_seq_1 (
    .WriteReg(S_WR), .RW(multiplexer_3_out), .Reset(Reset), .Clk(CLK), .Dados(multiplexer_13_out),
    .RA(multiplexer_3_out), .RB(S_RB), .DRA(S_DRA), .DRB(S_DRB));
  // Probe on S_DRA
  // Probe on S_DRB
  Multiplexer #(.width(8)) multiplexer_4 (.in0(V_DRA0), .in1(8'h4), .out(multiplexer_4_out), .sel(Inc));
  Multiplexer #(.width(8)) multiplexer_5 (.in0(V_DRA1), .in1(8'h4), .out(multiplexer_5_out), .sel(Inc));
  Multiplexer #(.width(8)) multiplexer_6 (.in0(V_DRA2), .in1(8'h4), .out(multiplexer_6_out), .sel(Inc));
  Multiplexer #(.width(8)) multiplexer_7 (.in0(V_DRA3), .in1(8'h4), .out(multiplexer_7_out), .sel(Inc));
  LED led_2 (.in(comparator_1_gt));
  Comparator comparator_1 (.a(S_DRA), .b({8{1'b0}}), .gt(comparator_1_gt), .eq(Zero), .lt(comparator_1_lt));
  LED led_3 (.in(comparator_1_lt));
  ULA ula_1 (.A(S_DRA), .B(S_DRB), .Funct(ALUOp), .S(ula_1_s));
  Move move_1 (.Imm(Imm), .R1(S_DRA), .MovH(move_1_movh), .MovL(move_1_movl));
  Multiplexer #(.width(8)) multiplexer_8 (.in0(move_1_movl), .in1(move_1_movh), .out(S_Mov), .sel(Sel_H));
  Move move_2 (.Imm(Imm), .R1(V_DRA0), .MovH(move_2_movh), .MovL(move_2_movl));
  ULA ula_2 (.A(multiplexer_4_out), .B(V_DRB0), .Funct(ALUOp), .S(ula_2_s));
  Move move_3 (.Imm(Imm), .R1(V_DRA1), .MovH(move_3_movh), .MovL(move_3_movl));
  ULA ula_3 (.A(multiplexer_5_out), .B(V_DRB1), .Funct(ALUOp), .S(ula_3_s));
  Move move_4 (.Imm(Imm), .R1(V_DRA2), .MovH(move_4_movh), .MovL(move_4_movl));
  ULA ula_4 (.A(multiplexer_6_out), .B(V_DRB2), .Funct(ALUOp), .S(ula_4_s));
  Move move_5 (.Imm(Imm), .R1(V_DRA3), .MovH(move_5_movh), .MovL(move_5_movl));
  ULA ula_5 (.A(multiplexer_7_out), .B(V_DRB3), .Funct(ALUOp), .S(ula_5_s));
  Multiplexer #(.width(8)) multiplexer_9 (.in0(move_2_movl), .in1(move_2_movh), .out(V_Mov0), .sel(Sel_H));
  Multiplexer #(.width(8)) multiplexer_10 (.in0(move_3_movl), .in1(move_3_movh), .out(V_Mov1), .sel(Sel_H));
  Multiplexer #(.width(8)) multiplexer_11 (.in0(move_4_movl), .in1(move_4_movh), .out(V_Mov2), .sel(Sel_H));
  Multiplexer #(.width(8)) multiplexer_12 (.in0(move_5_movl), .in1(move_5_movh), .out(V_Mov3), .sel(Sel_H));
  RAM MemDados_S (.addr(S_DRB), .we(S_WE), .oe(1'b1), .clk(CLK), .din(S_DRA), .dout(MemDados_S_dout));
  RAM #(.asyncread("true")) MemDados_V0 (
    .addr(V_DRB0), .we(V_WE), .oe(1'b1), .clk(CLK), .din(V_DRA0), .dout(MemDados_V0_dout));
  RAM #(.asyncread("true")) MemDados_V1 (
    .addr(V_DRB1), .we(V_WE), .oe(1'b1), .clk(CLK), .din(V_DRA1), .dout(MemDados_V1_dout));
  RAM #(.asyncread("true")) MemDados_V2 (
    .addr(V_DRB2), .we(V_WE), .oe(1'b1), .clk(CLK), .din(V_DRA2), .dout(MemDados_V2_dout));
  RAM #(.asyncread("true")) MemDados_V3 (
    .addr(V_DRB3), .we(V_WE), .oe(1'b1), .clk(CLK), .din(V_DRA3), .dout(MemDados_V3_dout));
  // Probe on multiplexer_13_out
  Multiplexer #(.select(2), .width(8)) multiplexer_13 (
    .in0(ula_1_s), .in1(MemDados_S_dout), .in2(S_Mov), .in3({8{1'b0}}), .out(multiplexer_13_out),
    .sel(DataToReg));
  Multiplexer #(.select(2), .width(8)) multiplexer_14 (
    .in0(ula_2_s), .in1(MemDados_V0_dout), .in2(V_Mov0), .in3({8{1'b0}}), .out(multiplexer_14_out),
    .sel(DataToReg));
  Multiplexer #(.select(2), .width(8)) multiplexer_15 (
    .in0(ula_3_s), .in1(MemDados_V1_dout), .in2(V_Mov1), .in3({8{1'b0}}), .out(multiplexer_15_out),
    .sel(DataToReg));
  Multiplexer #(.select(2), .width(8)) multiplexer_16 (
    .in0(ula_4_s), .in1(MemDados_V2_dout), .in2(V_Mov2), .in3({8{1'b0}}), .out(multiplexer_16_out),
    .sel(DataToReg));
  Multiplexer #(.select(2), .width(8)) multiplexer_17 (
    .in0(ula_5_s), .in1(MemDados_V3_dout), .in2(V_Mov3), .in3({8{1'b0}}), .out(multiplexer_17_out),
    .sel(DataToReg));
  // Probe on multiplexer_14_out
  // Probe on multiplexer_15_out
  // Probe on multiplexer_16_out
  // Probe on multiplexer_17_out

  // Notes on the sheet:
  //   contents of MemControle (hex, n*v repeats v):
  //   120 4 2a8 2a0 20 820 1020 400 110 2 258 250 10 810 11 1820
  //   contents of MemInstrucao (hex, n*v repeats v):
  //   d5 da df 55 5a 5f c8 cc 33 49 9e ea ef 31 59 fe 3a 7d 33 49 b8 cd 9e ea ef 31 20 59 fe 36 21 7d 33
  //   20 49 da c8 8e bc c9 86 cd bc a0 c9 9e d9 d9 ea 31 20 59 fe 35 22 7d 37 23 71
  //   PEs - Vetorial
  //   PE - Escalar
endmodule

module BR_seq (
  input  Reset,
  input  Clk,
  input  [7:0] Dados,
  input  WriteReg,
  input  [1:0] RW,
  input  [1:0] RA,
  input  [1:0] RB,
  output [7:0] DRA,
  output [7:0] DRB
);

  wire demultiplexer_1_out0, demultiplexer_1_out1, demultiplexer_1_out2, demultiplexer_1_out3;
  wire [7:0] SR1_q, SR2_q, SR3_q;

  Demultiplexer #(.select(2)) demultiplexer_1 (
    .out0(demultiplexer_1_out0), .out1(demultiplexer_1_out1), .out2(demultiplexer_1_out2),
    .out3(demultiplexer_1_out3), .in(WriteReg), .sel(RW));
  LED led_1 (.in(demultiplexer_1_out0));
  Register SR1 (.D(Dados), .en(demultiplexer_1_out1), .clk(Clk), .Q(SR1_q), .clr(Reset));
  Register SR2 (.D(Dados), .en(demultiplexer_1_out2), .clk(Clk), .Q(SR2_q), .clr(Reset));
  Register SR3 (.D(Dados), .en(demultiplexer_1_out3), .clk(Clk), .Q(SR3_q), .clr(Reset));
  Multiplexer #(.select(2), .width(8)) multiplexer_1 (
    .in0({8{1'b0}}), .in1(SR1_q), .in2(SR2_q), .in3(SR3_q), .out(DRA), .sel(RA));
  // Probe on DRA
  Multiplexer #(.select(2), .width(8)) multiplexer_2 (
    .in0({8{1'b0}}), .in1(SR1_q), .in2(SR2_q), .in3(SR3_q), .out(DRB), .sel(RB));
  // Probe on DRB
endmodule

module BR_vet (
  input  Reset,
  input  Clk,
  input  [7:0] Dados,
  input  [7:0] VR0,
  input  WriteReg,
  input  [1:0] RW,
  input  [1:0] RA,
  input  [1:0] RB,
  output [7:0] DRA,
  output [7:0] DRB
);

  wire demultiplexer_1_out0, demultiplexer_1_out1, demultiplexer_1_out2, demultiplexer_1_out3;
  wire [7:0] VR1_q, VR2_q, VR3_q;

  LED led_1 (.in(demultiplexer_1_out0));
  Demultiplexer #(.select(2)) demultiplexer_1 (
    .out0(demultiplexer_1_out0), .out1(demultiplexer_1_out1), .out2(demultiplexer_1_out2),
    .out3(demultiplexer_1_out3), .in(WriteReg), .sel(RW));
  Register VR1 (.D(Dados), .en(demultiplexer_1_out1), .clk(Clk), .Q(VR1_q), .clr(Reset));
  Register VR2 (.D(Dados), .en(demultiplexer_1_out2), .clk(Clk), .Q(VR2_q), .clr(Reset));
  Register VR3 (.D(Dados), .en(demultiplexer_1_out3), .clk(Clk), .Q(VR3_q), .clr(Reset));
  Multiplexer #(.select(2), .width(8)) multiplexer_1 (
    .in0(VR0), .in1(VR1_q), .in2(VR2_q), .in3(VR3_q), .out(DRA), .sel(RA));
  // Probe on DRA
  Multiplexer #(.select(2), .width(8)) multiplexer_2 (
    .in0(VR0), .in1(VR1_q), .in2(VR2_q), .in3(VR3_q), .out(DRB), .sel(RB));
  // Probe on DRB
endmodule

module ULA (
  input  [7:0] A,
  input  [7:0] B,
  input  [1:0] Funct,
  output [7:0] S
);

  wire adder_1_cout, subtractor_1_bout;
  wire [0:0] D3;
  wire [7:0] D0, D1, D2;

  Adder adder_1 (.a(A), .b(B), .out(D0), .cin(1'b0), .cout(adder_1_cout));
  Subtractor subtractor_1 (.a(A), .b(B), .out(D1), .bin(1'b0), .bout(subtractor_1_bout));
  assign D2 = A & B;  // AND_Gate and_1, 8 bits wide
  LED led_1 (.in(adder_1_cout));
  LED led_2 (.in(subtractor_1_bout));
  nor nor_1 (D3[0], B[0], B[1], B[2], B[3], B[4], B[5], B[6], B[7]);
  Multiplexer #(.select(2), .width(8)) multiplexer_1 (
    .in0(D0), .in1(D1), .in2(D2), .in3({{7{1'b0}}, D3[0]}), .out(S), .sel(Funct));

  // Notes on the sheet:
  //   A + B
  //   A - B
  //   A and B
  //   not B
endmodule

module Decodificador (
  input  [7:0] Inst,
  output [3:0] Imm,
  output [1:0] S_RA,
  output [1:0] V_RA,
  output [1:0] S_RB,
  output [1:0] V_RB,
  output [3:0] Opcode
);

  wire and_1_out, and_2_out, and_3_out, or_1_out, or_2_out;

  and and_1 (and_1_out, ~Inst[4], Inst[7]);  // AND_Gate
  and and_2 (and_2_out, ~Inst[5], Inst[7]);  // AND_Gate
  and and_3 (and_3_out, ~Inst[6], Inst[7]);  // AND_Gate
  or or_1 (or_1_out, and_1_out, and_2_out);
  or or_2 (or_2_out, or_1_out, and_3_out);
  Demultiplexer #(.width(2)) demultiplexer_1 (.out0(S_RA), .out1(V_RA), .in(Inst[3:2]), .sel(or_2_out));
  Demultiplexer #(.width(2)) demultiplexer_2 (.out0(S_RB), .out1(V_RB), .in(Inst[1:0]), .sel(or_2_out));

  assign Imm = Inst[3:0];
  assign Opcode = Inst[7:4];
endmodule

module Move (
  input  [3:0] Imm,
  input  [7:0] R1,
  output [7:0] MovH,
  output [7:0] MovL
);


  assign MovH = {Imm, R1[3:0]};
  assign MovL = {R1[7:4], Imm};
endmodule
